# Fritzing sketch two_way_communication (saved by Fritzing 0.9.4)
breadboards: 1

parts:
  Part1 = Adafruit HUZZAH32 ESP32 Feather [part_number="Adafruit #3405"]
  S1 = Momentary Switch [package=tactile-pth]
  LED1 = smd LED [color="Red (633nm)" package="1206 [SMD]"]

nets:
  N1: Part1.A5_IO4, Part1.GND, LED1.anode
  N2: Part1.A4_IO36, LED1.cathode
  N3: Part1.A0_DAC2, S1.2
  N4: Part1.3.3V, S1.1
